# Fritzing sketch Arduino (saved by Fritzing 0.7.12b)
breadboards: 2

parts:
  Arduino1 = Arduino
  T1 = LM35 Temperature Sensor [package="TO92 [THT]"]
  T2 = TMP36 Temperature Sensor [package="TO92 [THT]"]
  S1 = Pushbutton [package="[THT]"]
  S2 = Pushbutton [package="[THT]"]
  S3 = Pushbutton [package="[THT]"]
  R1 = 1k Ω Resistor [package=THT]
  R2 = 1k Ω Resistor [package=THT]
  R3 = 1k Ω Resistor [package=THT]
  LCD1 = LCD screen
  LED2 = LED - 5mm [color="Red (633nm)" package="5 mm [THT]"]
  R4 = Resistor [tolerance=±5% resistance=220 package=THT]
  R6 = Resistor [tolerance=±5% resistance=220 package=THT]
  R7 = Resistor [tolerance=±5% resistance=220 package=THT]
  R8 = Resistor [tolerance=±5% resistance=220 package=THT]
  R9 = 4.7k Ω Resistor [package=THT]
  R10 = 100 Ω Resistor [package=THT]
  R12 = 100 Ω Resistor [package=THT]
  R13 = 1k Ω Resistor [package=THT]
  R14 = 1k Ω Resistor [package=THT]
  R11 = 10 Ω Resistor [package=THT]
  BS1 = BASIC Stamp 2p24  # not connected
  D1 = Rectifier Diode [part_number=1N4001 package="300 mil [THT]"]
  M1 = DC Motor  # not connected
  VCC1 = Battery block 9V  # not connected
  S4 = Toggle Switch [package=THT]

nets (from the schematic view):
  GND: Arduino1.GND, T1.GND, R2.Pin_0, R13.Pin_1, S4.L1
  N1: Arduino1.D13, Arduino1.A4, S1.Pin_3, S1.Pin_4, R3.Pin_1
  N2: Arduino1.D11, Arduino1.A2, LCD1.E
  N3: Arduino1.D10, Arduino1.D8, S3.Pin_1, S3.Pin_2, R1.Pin_0
  N4: Arduino1.D9, R6.Pin_1
  N5: Arduino1.D7, Arduino1.D4, Arduino1.A5, LCD1.DB5, R4.Pin_0
  N6: Arduino1.D6, R2.Pin_1
  N7: Arduino1.D5, LCD1.DB4
  N8: Arduino1.D3, LCD1.DB6
  N9: Arduino1.D2, LCD1.DB7
  N10: Arduino1.D1TX, S4.COM
  N11: Arduino1.+5V, T1.+Vs, T2.+Vs, S3.Pin_3, S3.Pin_4, R7.Pin_1
  N12: Arduino1.A0, T2.Vout
  N13: Arduino1.A1, T1.Vout
  N14: Arduino1.A3, LCD1.RS
  N15: T2.GND, R14.Pin_1
  N16: S1.Pin_1, S1.Pin_2
  N17: S2.Pin_1, S2.Pin_2
  N18: S2.Pin_3, S2.Pin_4
  VSS: LCD1.VSS, LCD1.VDD
  N19: LCD1.V0, R8.Pin_1, R9.Pin_1
  N20: LCD1.LED+, R6.Pin_0
  N21: LCD1.LED-, D1.anode
  N22: LED2.anode, R4.Pin_1
  N23: R7.Pin_0, R9.Pin_0
  N24: R8.Pin_0, R10.Pin_1, R12.Pin_1
  N25: R10.Pin_0, R12.Pin_0, R11.Pin_0
  N26: R13.Pin_0, R14.Pin_0, R11.Pin_1
